// Logisim project Components.circ as structural Verilog: 4 circuits, main circuit Instruction Decoder
module Data_Path (
  input  in_1,
  input  in_2
);


  // Other names for the same wires on the sheet: CLk = in_1; Reset = in_2
endmodule

module Instruction_Decoder (
  input  [31:0] in_1,
  output [5:0] out_2,
  output [25:0] out_3,
  output [4:0] out_4,
  output [4:0] out_5,
  output [15:0] out_6,
  output [4:0] out_7,
  output [5:0] out_8
);


  assign out_2 = in_1[31:26];
  assign out_3 = in_1[25:0];
  assign out_4 = in_1[20:16];
  assign out_5 = in_1[25:21];
  assign out_6 = in_1[15:0];
  assign out_7 = in_1[15:11];
  assign out_8 = in_1[5:0];

  // Other names for the same wires on the sheet: Constante[15:0] = in_1[15:0]; Destino_Salto[25:0] = in_1[25:0];
  //   Func_Code[5:0] = in_1[5:0]; Rd[4:0] = in_1[15:11]; Rs[4:0] = in_1[20:16]; Rt[4:0] = in_1[25:21];
  //   Op_Code[5:0] = in_1[31:26]

  // Notes on the sheet:
  //   Instruction Decoder
  //   Outputs
endmodule

module Program_Counter (
  input  [31:0] in_1,
  input  [31:0] in_2,
  input  PC_Enable,
  input  CLK,
  input  Reset
);

  Register #(.width(32)) register_1 (.D(in_1), .en(PC_Enable), .Q(in_2), .clk(CLK), .clr(Reset));

  // Notes on the sheet:
  //   PC' (next instruction)
  //   Program Counter
  //   PC (current instruction)
endmodule

module Litte_Endian___Big_Endian (
  input  [31:0] in_1,
  output [31:0] out_2
);


  assign out_2 = {in_1[7:0], in_1[15:8], in_1[23:16], in_1[31:24]};

  // Notes on the sheet:
  //   Input
  //   Output
endmodule
